# Fritzing sketch Arduino_mega_Joystick_Receiver (saved by Fritzing 0.9.0b)

parts:
  NRF24L1 = NRF24L01
  NRF24L2 = NRF24L01  # not connected
  Componente4 = Arduino Mega 2560 (Rev3)

nets:
  VCC: NRF24L1.VCC, Componente4.3V3
  N1: NRF24L1.CSN, Componente4.D10_PWM
  N2: NRF24L1.MOSI, Componente4.D51
  GND: NRF24L1.GND, Componente4.GND
  N3: NRF24L1.CE, Componente4.D9_PWM
  N4: NRF24L1.SCK, Componente4.D52
  N5: NRF24L1.MISO, Componente4.D50

notes:
  GND = Black
  VCC = Red
  CE = Yellow
  CSN = Green
  SCK = Orange
  MOSI = White
  MISO = Brown
  IRQ = Not Connected
  This connection are intended looking the TOP of the NRF24L01(as image suggested)
  if you "t u r n" the NRF24L01 upsidedown , take care to not invert some wire
  Arduino MEGA could be unstable on
  3.3 V output, so you have some problem , try to correct the ripple placing a 10uF capacitor.
  Usefull information on:
  http://arduino-info.wikispaces.com/Nrf24L01-2.4GHz-HowTo

custom parts:
  NRF24L01: NRF24L01 module
