# Fritzing sketch Arduino_Joystick_Receiver (saved by Fritzing 0.9.0b)

parts:
  NRF24L1 = NRF24L01
  Componente1 = Arduino Uno (Rev3) - ICSP
  NRF24L2 = NRF24L01  # not connected

nets:
  VCC: NRF24L1.VCC, Componente1.3V3
  N1: NRF24L1.CSN, Componente1.D10_PWM/SS
  N2: NRF24L1.MOSI, Componente1.ICSP_MOSI, Componente1.D11_PWM/MOSI
  GND: NRF24L1.GND, Componente1.GND
  N3: NRF24L1.CE, Componente1.D9_PWM
  N4: NRF24L1.SCK, Componente1.D13/SCK
  N5: NRF24L1.MISO, Componente1.ICSP_MISO, Componente1.D12/MISO

notes:
  GND = Black
  VCC = Red
  CE = Yellow
  CSN = Green
  SCK = Orange
  MOSI = White
  MISO = Brown
  IRQ = Not Connected
  This connection are intended looking the TOP of the NRF24L01(as image suggested)
  if you "t u r n" the NRF24L01 upsidedown , take care to not invert some wire

custom parts:
  NRF24L01: NRF24L01 module
