# Fritzing sketch Arduino_Nano_Control_Device (saved by Fritzing 0.9.0b)
breadboards: 1

parts:
  BUTTON1 = Arcade Button (red)
  BUTTON3 = Arcade Button (green)
  BUTTON4 = Arcade Button (white)
  R1 = Resistor [tolerance=±5% resistance=10k package=THT]
  R2 = Resistor [tolerance=±5% resistance=10k package=THT]
  R3 = Resistor [tolerance=±5% resistance=10k package=THT]
  R4 = Slide Potentiometer [maximum_resistance=100kΩ]
  Componente2 = Arduino Nano (Rev3.0)

nets:
  N1: BUTTON1.no_name_yet#1, R2.Pin_1, Componente2.D3
  N2: BUTTON1.no_name_yet#2, BUTTON3.no_name_yet#2, BUTTON4.no_name_yet#2, Componente2.GND
  N3: BUTTON3.no_name_yet#1, R1.Pin_1
  N4: BUTTON4.no_name_yet#1, R3.Pin_1, Componente2.D4
  N5: R1.Pin_0, R2.Pin_0, R3.Pin_0, R4.leg1, R4.leg2, Componente2.5V
  N6: R4.wiper, Componente2.A0

notes:
  Slide Resistors
  500K (log)
  R1 = R2 = R3 = 10K
  Buttons

custom parts:
  Arcade Button (red): Adafruit Arcade Button (red)
  Arcade Button (green): Adafruit Arcade Button (green)
  Arcade Button (white): Adafruit Arcade Button (white)
