# Fritzing sketch Arduino_VoiceRecognition (saved by Fritzing 0.8.7b)
breadboards: 1

parts:
  Componente1 = Arduino Uno (Rev3) - ICSP  # not connected
  U1 = XBee
  T1 = DS18B20 Temperature Sensor [part_number=DS18B20 package="TO92 [THT]"]
  R1 = Resistor [tolerance=±5% resistance=4.7k package=THT]
  R2 = PHOTOCELL [package=photocell]
  R3 = Resistor [tolerance=±5% resistance=10k package=THT]

nets:
  N1: U1.GND, T1.+Vdd, R2.P$1
  N2: T1.DQ, R1.Pin_0
  N3: T1.GND, R1.Pin_1, R3.Pin_1
  N4: R2.P$2, R3.Pin_0

notes:
  EASYVR Shild
  need to be mounted on an Arduino
  DS18B20
  Resistor pull-up 4.7 K
  Photoresistor
  Resistor pull-up 10 K

custom parts:
  XBee: XBee embedded RF module.
  DS18B20 Temperature Sensor: A DS18B20 temperature sensor
