# Fritzing sketch CurrentProbe (saved by Fritzing 0.8.3b)
breadboards: 1

parts:
  RaspberryPi1 = Raspberry Pi Model B
  IC1 = MCP3008 8-channel 10-bit ADC [part_number=MCP3008]
  C1 = Electrolytic Capacitor [capacitance=10µF voltage=10V package="1010 [SMD, electrolytic]"]
  R2 = Resistor [tolerance=±5% resistance=470k package=THT]
  R3 = Resistor [tolerance=±5% resistance=470k package=THT]
  R4 = Resistor [tolerance=±5% resistance=10k package=THT]
  R5 = Resistor [tolerance=±5% resistance=10k package=THT]

nets:
  N1: RaspberryPi1.5V, IC1.no_name_yet#16, R3.Pin_1
  N2: RaspberryPi1.GND, IC1.no_name_yet#9, C1.-, R2.Pin_0, R5.Pin_0
  N3: RaspberryPi1.MOSI, IC1.no_name_yet#11
  N4: RaspberryPi1.MISO, IC1.no_name_yet#12
  N5: RaspberryPi1.SCLK, IC1.no_name_yet#13
  N6: RaspberryPi1.CS0, IC1.no_name_yet#10
  N7: IC1.no_name_yet#1, R4.Pin_0, R5.Pin_1
  N8: IC1.no_name_yet#15, C1.+, R2.Pin_1, R3.Pin_0, R4.Pin_1

notes:
  R2 = R3 = 560K
  R4 = R5 = 10K
  Connect SCT013
  30A / 1V

custom parts:
  Raspberry Pi Model B: Raspberry Pi (Model B)
