# Fritzing sketch GAS (saved by Fritzing 0.8.3b)
breadboards: 1

parts:
  Componente1 = Gas Sensor Breakout Board
  Terminal1 = Banana Connector
  Terminal2 = Banana Connector
  R1 = Rotary Potentiometer (Small)
  Terminal3 = Banana Connector
  Terminal4 = Banana Connector

nets:
  N1: Componente1.H1, Componente1.A1, Terminal2.Female_Bannana_Connector
  N2: Componente1.GND, Terminal1.Female_Bannana_Connector, R1.wiper, Terminal3.Female_Bannana_Connector
  N3: Componente1.B1, R1.leg1, Terminal4.Female_Bannana_Connector

notes:
  +5 V
  GND
  H
  A
  47 K OHM
  Multimeter

custom parts:
  Banana Connector: A Banana connector useful for power inputs on the bread board etc
  Banana Connector: A Banana connector useful for power inputs on the bread board etc
