# Fritzing sketch rele_passo_passo_con_raspberry_V1_2 (saved by Fritzing 0.8.3b)
breadboards: 3

parts:
  Raspberry_Pi_rev1 = Raspberry Pi rev2
  Q1 = NPN-Transistor [package="TO92 [THT]"]
  Q2 = NPN-Transistor [package="TO92 [THT]"]
  R1 = Resistor [package="0402 [SMD]"]
  R2 = Resistor [package="0402 [SMD]"]
  JP1 = Header 3 [package=screwterminal-3.5mm-3_lock.007s]
  JP2 = Header 10 [package=1x10-2mm-smd]
  K5 = Relay [part_number=FRS1B-S package=THT]
  K6 = Relay [part_number=FRS1B-S package=THT]
  K7 = Relay [part_number=FRS1B-S package=THT]
  K8 = Relay [part_number=FRS1B-S package=THT]
  R3 = Resistor [package="0402 [SMD]"]
  R4 = Resistor [package="0402 [SMD]"]
  R5 = Resistor [package="0402 [SMD]"]
  R6 = Resistor [package="0402 [SMD]"]
  Power_plug1 = Power plug
  Power_plug2 = Power plug
  CNY74-1 = CNY74-4 [package="DIP (Dual Inline) [THT]"]
  K9 = Relay 2 x switch [part_number=351 package=THT]
  K10 = Relay 2 x switch [part_number=351 package=THT]
  S1 = Square Pushbutton
  S2 = Square Pushbutton
  R7 = Resistor [package="0402 [SMD]"]
  R8 = Resistor [package="0402 [SMD]"]
  R9 = Resistor [package="0402 [SMD]"]
  R10 = Resistor [package="0402 [SMD]"]
  K11 = Relay 2 x switch [part_number=351 package=THT]
  S3 = Toggle Switch [package=THT]
  R11 = Resistor [package="0402 [SMD]"]
  R12 = Resistor [package="0402 [SMD]"]

nets:
  N1: Raspberry_Pi_rev1.5V, Q1.C, Q2.C, R1.Pin_0, R2.Pin_0
  N2: Raspberry_Pi_rev1.GIPO_2, Q1.B, R1.Pin_1
  N3: Raspberry_Pi_rev1.GIPO_3, Q2.B, R2.Pin_1
  N4: Raspberry_Pi_rev1.GND, Q1.E, Q2.E, JP1.1, JP1.2, JP1.3
  N5: JP2.5, CNY74-1.C3, R12.Pin_1
  N6: JP2.6, CNY74-1.C1, R11.Pin_1
  N7: JP2.7, R4.Pin_1, CNY74-1.E2
  N8: JP2.8, R3.Pin_1, CNY74-1.E0
  N9: JP2.9, R3.Pin_0, R4.Pin_0, R5.Pin_1, R6.Pin_1, Power_plug2.GND, R9.Pin_1, R10.Pin_1, R11.Pin_0, R12.Pin_0
  N10: JP2.10, Power_plug2.VCC, CNY74-1.E3, CNY74-1.C2, CNY74-1.E1, CNY74-1.C0, K9.pin_11, K10.pin_11, K11.pin_8, K11.pin_9
  N11: K5.C2, K6.C2, K7.C2, K8.C1, K8.C2, Power_plug1.GND, S1.leg0, S2.leg0, R7.Pin_0, R8.Pin_0, K11.pin_4
  N12: K5.B, K10.pin_13
  N13: K6.B, K9.pin_13
  N14: R5.Pin_0, CNY74-1.K0
  N15: R6.Pin_0, CNY74-1.K2
  N16: Power_plug1.VCC, K9.pin_4, K10.pin_4, S3.COM
  N17: CNY74-1.A0, K10.pin_9
  N18: CNY74-1.K1, R7.Pin_1
  N19: CNY74-1.A1, R10.Pin_0
  N20: CNY74-1.A5, K9.pin_9
  N21: CNY74-1.K3, R8.Pin_1
  N22: CNY74-1.A3, R9.Pin_0
  N23: S1.leg1, K11.pin_6
  N24: S2.leg1, K11.pin_11
  N25: K11.pin_13, S3.L1

notes:
  12V ac
  pull down resistor
  2M OHM
  resistor 100K OHM
  5V cc
  to the lamp
  to Fase
  Box for by-pass domotics
  Switch for by-pass Domotics

custom parts:
  CNY74-4: 4way optocoupler
  Relay 2 x switch: An DPDT relay. 2 x switch, same footprint as G5 V-2 Omron or V23042 Siemens
