# Fritzing sketch Wall_switch (saved by Fritzing 0.8.7b)
breadboards: 1

parts:
  IC1 = MCP23017 I2C I/O Expander
  S1 = Square Pushbutton
  S2 = Square Pushbutton
  LED2 = LEDs [package=led10mm]  # not connected
  LED3 = LEDs [package=led10mm]  # not connected
  LED4 = LEDs [package=led10mm]  # not connected
  LED5 = LEDs [package=led10mm]  # not connected
  LED6 = LEDs [package=led10mm]  # not connected
  LED7 = LEDs [package=led10mm]  # not connected
  LED8 = LEDs [package=led10mm]  # not connected
  LED9 = LEDs [package=led10mm]  # not connected
  LED10 = LEDs [package=led10mm]  # not connected
  LED11 = LEDs [package=led10mm]
  R1 = 50 Ω Resistor [package=THT]
  R2 = Resistor [tolerance=±5% resistance=220 package=THT]
  R3 = 50 Ω Resistor [package=THT]  # not connected
  R4 = Resistor [tolerance=±5% resistance=220 package=THT]  # not connected
  R5 = 50 Ω Resistor [package=THT]
  R6 = 50 Ω Resistor [package=THT]
  R7 = 50 Ω Resistor [package=THT]
  R8 = 50 Ω Resistor [package=THT]
  R9 = Resistor [tolerance=±5% resistance=220 package=THT]
  R10 = Resistor [tolerance=±5% resistance=220 package=THT]
  R11 = Resistor [tolerance=±5% resistance=220 package=THT]
  R12 = Resistor [tolerance=±5% resistance=220 package=THT]
  S3 = Square Pushbutton
  S4 = Square Pushbutton
  S5 = Square Pushbutton
  Raspberry_Pi_rev1 = Raspberry Pi B rev2

nets:
  N1: IC1.GPB0, R12.Pin_1
  N2: IC1.GPB1, R8.Pin_1
  N3: IC1.GPB2, R11.Pin_1
  N4: IC1.GPB3, R7.Pin_1
  N5: IC1.GPB4, R10.Pin_1
  N6: IC1.GPB5, R6.Pin_1
  N7: IC1.GPB6, R9.Pin_1
  N8: IC1.GPB7, R5.Pin_1
  VDD: IC1.VDD, IC1.A2, IC1.RESET, LED11.C, Raspberry_Pi_rev1.5V
  VSS: IC1.VSS, IC1.A0, IC1.A1, S5.leg0, Raspberry_Pi_rev1.GND
  N9: IC1.SCL, Raspberry_Pi_rev1.GPIO_3
  N10: IC1.SDA, Raspberry_Pi_rev1.GPIO_2
  N11: IC1.GPA1, S5.leg1
  N12: IC1.GPA2, S4.leg1
  N13: IC1.GPA3, S3.leg1
  N14: IC1.GPA4, S2.leg1
  N15: IC1.GPA5, S1.leg1
  N16: IC1.GPA6, R1.Pin_1
  N17: IC1.GPA7, R2.Pin_1

notes:
  this configuration set address = 24
  Set PullUp resistors by software for inputs
  R1 = 1000 OHM
  R2 = 270 OHM
  use http://led.linear1.org/1led.wiz to calcolate resistor
  REMEMBER max 25 mA each output pin for MCP23017 as specified in Datasheet (http://ww1.microchip.com/downloads/en/DeviceDoc/21952b.pdf)
  R1 = 1000 OHM for RED LED
  R2 = 270 OHM for GREEN LED
  B
  A

custom parts:
  MCP23017 I2C I/O Expander: MCP23017 I2C 16-Channel I/O Expander
  50 Ω Resistor: A generic resistor (0.25W)
