# Fritzing sketch Raspberry_mpc3008_NTC_termistors (saved by Fritzing 0.8.3b)
breadboards: 1

parts:
  IC1 = MCP3008 8-channel 10-bit ADC [part_number=MCP3008]
  Raspberry_Pi_rev1 = Raspberry Pi rev2
  R1 = Temperature Sensor (Thermistor) [thermistor_type=NTC package=THT]
  R2 = Temperature Sensor (Thermistor) [thermistor_type=NTC package=THT]  # not connected
  R3 = Temperature Sensor (Thermistor) [thermistor_type=NTC package=THT]
  R4 = Temperature Sensor (Thermistor) [thermistor_type=NTC package=THT]
  R5 = Resistor [tolerance=±5% resistance=220 package=THT]
  R6 = Resistor [tolerance=±5% resistance=220 package=THT]
  R7 = Resistor [tolerance=±5% resistance=220 package=THT]
  R8 = Resistor [tolerance=±5% resistance=220 package=THT]

nets:
  N1: IC1.no_name_yet#1, IC1.no_name_yet#2, IC1.no_name_yet#3, IC1.no_name_yet#5, IC1.no_name_yet#9, IC1.no_name_yet#14, Raspberry_Pi_rev1.GND, R1.pin_1, R3.pin_1, R4.pin_1, R5.Pin_0, R6.Pin_0, R7.Pin_0, R8.Pin_0
  N2: IC1.no_name_yet#10, Raspberry_Pi_rev1.GPIO_8
  N3: IC1.no_name_yet#11, Raspberry_Pi_rev1.GPIO_10
  N4: IC1.no_name_yet#12, Raspberry_Pi_rev1.GPIO_9
  N5: IC1.no_name_yet#13, Raspberry_Pi_rev1.GPIO_11
  N6: IC1.no_name_yet#15, IC1.no_name_yet#16, Raspberry_Pi_rev1.3V3, R1.pin_0, R3.pin_0, R4.pin_0, R5.Pin_1, R6.Pin_1, R7.Pin_1, R8.Pin_1

notes:
  Resistors 39K OHM
