# Fritzing sketch Board (saved by Fritzing 0.8.3b)
breadboards: 1

parts:
  IC2 = MCP23017 I2C I/O Expander  # not connected
  IC3 = MCP3008 8-channel 10-bit ADC [part_number=MCP3008]
  PWM1 = PCA9685 16x12-bit PWM Breakout
  J1 = Basic Servo
  R1 = Temperature Sensor (Thermistor) [thermistor_type=NTC package=THT]  # not connected
  R2 = 50 Ω Resistor [package=THT]  # not connected
  R3 = Rotary Potentiometer (Large) [maximum_resistance=100kΩ package=THT]  # not connected
  S4 = Round Pushbutton  # not connected
  Pi1 = Adafruit Pi Cobbler
  Terminal1 = Banana Connector
  Terminal2 = Banana Connector
  J2 = Basic Servo
  U1 = GAS_SENSOR [package=mq-3]  # not connected
  S5 = Round Pushbutton

nets:
  N1: IC3.no_name_yet#10, Pi1.CE0
  N2: PWM1.no_name_yet#0, J1.pulse
  N3: PWM1.no_name_yet#4, J2.pulse
  N4: PWM1.no_name_yet#100, PWM1.no_name_yet#104, PWM1.no_name_yet#706, Terminal1.Female_Bannana_Connector
  N5: PWM1.no_name_yet#701, PWM1.no_name_yet#1000, PWM1.no_name_yet#1004, Pi1.GND, Terminal2.Female_Bannana_Connector
  N6: Pi1.PIN20, S5.leg0
  N7: Pi1.#25, S5.leg1

notes:
  Servo 0
  Servo 4
  +5 Vcc
  GND
  Solded A2 (address 44)
  MQ 2 (gas sensor)
  Shutdown
  button
  PAY ATTENTION
  NO +5V in this SIDE

custom parts:
  MCP23017 I2C I/O Expander: MCP23017 I2C 16-Channel I/O Expander
  50 Ω Resistor: A generic resistor (0.25W)
  Adafruit Pi Cobbler: Adafruit Pi Cobbler GPIO Breakout for Raspberry Pi
  Banana Connector: A Banana connector useful for power inputs on the bread board etc
  Banana Connector: A Banana connector useful for power inputs on the bread board etc
