# Fritzing sketch Board2 (saved by Fritzing 0.8.3b)
breadboards: 1

parts:
  IC2 = MCP23017 I2C I/O Expander
  IC3 = MCP3008 8-channel 10-bit ADC [part_number=MCP3008]
  PWM1 = PCA9685 16x12-bit PWM Breakout
  J1 = Basic Servo
  R1 = Temperature Sensor (Thermistor) [thermistor_type=NTC package=THT]
  R2 = 50 Ω Resistor [package=THT]
  R3 = Rotary Potentiometer (Large) [maximum_resistance=100kΩ package=THT]
  S4 = Round Pushbutton
  Pi1 = Adafruit Pi Cobbler
  Terminal1 = Banana Connector
  Terminal2 = Banana Connector
  J2 = Basic Servo
  U1 = GAS_SENSOR [package=mq-3]
  S5 = Round Pushbutton
  R4 = Temperature Sensor (Thermistor) [thermistor_type=NTC package=THT]
  R5 = Temperature Sensor (Thermistor) [thermistor_type=NTC package=THT]
  R6 = Temperature Sensor (Thermistor) [thermistor_type=NTC package=THT]
  R7 = 50 Ω Resistor [package=THT]
  R8 = 50 Ω Resistor [package=THT]
  R9 = 50 Ω Resistor [package=THT]
  Terminal3 = Banana Connector
  S6 = Round Pushbutton
  S7 = Round Pushbutton
  S8 = Round Pushbutton

nets:
  VDD: IC2.VDD, IC2.A2, IC2.RESET, IC3.no_name_yet#15, IC3.no_name_yet#16, PWM1.no_name_yet#605, R1.pin_1, Pi1.3V3, R4.pin_1, R5.pin_1, R6.pin_0
  VSS: IC2.VSS, IC2.A0, IC2.A1, IC3.no_name_yet#9, IC3.no_name_yet#14, PWM1.no_name_yet#601, PWM1.no_name_yet#701, PWM1.no_name_yet#1000, PWM1.no_name_yet#1004, R2.Pin_0, R3.wiper, S4.leg0, Pi1.GND, Terminal2.Female_Bannana_Connector, U1.H1, R7.Pin_0, R8.Pin_0, R9.Pin_0, S6.leg0, S7.leg1, S8.leg1
  N1: IC2.SCL, PWM1.no_name_yet#603, Pi1.SCL0
  N2: IC2.SDA, PWM1.no_name_yet#604, Pi1.SDA0
  N3: IC2.GPA4, S8.leg0
  N4: IC2.GPA5, S7.leg0
  N5: IC2.GPA6, S6.leg1
  N6: IC2.GPA7, S4.leg1
  N7: IC3.no_name_yet#1, R1.pin_0, R2.Pin_1
  N8: IC3.no_name_yet#2, R4.pin_0, R7.Pin_1
  N9: IC3.no_name_yet#3, R5.pin_0, R8.Pin_1
  N10: IC3.no_name_yet#4, R6.pin_1, R9.Pin_1
  N11: IC3.no_name_yet#5, R3.leg2, U1.H2
  N12: IC3.no_name_yet#10, Pi1.CE0
  N13: IC3.no_name_yet#11, Pi1.MOSI
  N14: IC3.no_name_yet#12, Pi1.MISO
  N15: IC3.no_name_yet#13, Pi1.SCLK
  N16: PWM1.no_name_yet#0, J1.pulse
  N17: PWM1.no_name_yet#4, J2.pulse
  N18: PWM1.no_name_yet#100, PWM1.no_name_yet#104, PWM1.no_name_yet#706, Terminal1.Female_Bannana_Connector
  N19: Pi1.PIN20, S5.leg0
  N20: Pi1.#25, S5.leg1
  N21: U1.B1, U1.A1, Terminal3.Female_Bannana_Connector

notes:
  Servo 0
  Servo 4
  +5 Vcc
  GND
  Solded A2 (address 44)
  MQ 2 (gas sensor)
  Shutdown
  button
  Termistor 1
  Termistor 2
  Termistor 3
  Termistor 4
  R1,R2,R3,R4 = 39 K OHM
  MCP23017
  Address 24<module fritzingVersion="0.8.3b.07.27.048f">
  <boundingRects>
  <boundingRect rect="0 0 0 0" name="Vista schema"/>
  <boundingRect rect="611.462 95 84.0769 41" name="Vista Breadboard"/>
  <boundingRect rect="0 0 0 0" name="Vista PCB"/>
  </boundingRects>
  <instances>
  <instance moduleIdRef="NoteModuleID" modelIndex="1775473" path=":/resources/parts/core/note.fzp">
  <text>&lt;!DOCTYPE HTML PUBLIC "-//W3C//DTD HTML 4.0//EN" "http://www.w3.org/TR/REC-html40/strict.dtd">
  &lt;html>&lt;head>&lt;meta name="qrichtext" content="1" />&lt;style type="text/css">
  p, li { white-space: pre-wrap; }
  &lt;/style>&lt;/head>&lt;body style=" font-family:'Droid Sans'; font-size:9pt; font-weight:400; font-style:normal;">
  &lt;p style=" margin-top:0px; margin-bottom:0px; margin-left:0px; margin-right:0px; -qt-block-indent:0; text-indent:0px;">Button 0&lt;/p>&lt;/body>&lt;/html></text>
  <views>
  <breadboardView layer="breadboardNote">
  <geometry width="84.0769" x="611.462" y="95" z="7.00057" height="41"/>
  </breadboardView>
  </views>
  </instance>
  </instances>
  </module>
  Button 0
  Button 1
  Button 2
  Button 3

custom parts:
  MCP23017 I2C I/O Expander: MCP23017 I2C 16-Channel I/O Expander
  50 Ω Resistor: A generic resistor (0.25W)
  Adafruit Pi Cobbler: Adafruit Pi Cobbler GPIO Breakout for Raspberry Pi
  Banana Connector: A Banana connector useful for power inputs on the bread board etc
  Banana Connector: A Banana connector useful for power inputs on the bread board etc
