# Fritzing sketch Raspberry_DS18B20_temperature (saved by Fritzing 0.8.3b)
breadboards: 1

parts:
  Raspberry_Pi_rev1 = Raspberry Pi rev2
  R1 = Resistor [tolerance=±5% resistance=4.7k package=THT]
  part = NPN-Transistor [part_number=DS18B20 package="TO92 [THT]"]

nets:
  3V3: Raspberry_Pi_rev1.3V3, Raspberry_Pi_rev1.5V, R1.Pin_1, part.C
  N1: Raspberry_Pi_rev1.GND, part.E
  N2: Raspberry_Pi_rev1.GPIO_23, R1.Pin_0, part.B
